# Fritzing sketch lueftung (saved by Fritzing 0.9.0b)
circuit board: 11.5775cm x 6.77326cm
breadboards: 2

parts:
  LCD1 = LCD screen
  R2 = Resistor [tolerance=±5% resistance=220 package=THT]
  Bauteil2 = Arduino Nano (Rev3.0)
  J1 = screw terminal, 2 pins [part_number="Power in"]
  J2 = screw terminal, 4 pins [part_number=VCC]
  J3 = screw terminal, 4 pins [part_number=GND]
  J4 = screw terminal, 4 pins [part_number=1W]
  R3 = Resistor [tolerance=±5% resistance=220 package=THT]
  LED2 = LED - 3mm [color="Green (570nm)" package="3 mm [THT]"]
  LED1 = LED - 3mm [color="Red (633nm)" package="3 mm [THT]"]
  R4 = Resistor [tolerance=±5% resistance=220 package=THT]
  R5 = Resistor [tolerance=±5% resistance=220 package=THT]
  U1 = mystery part, 5 pins [chip_label=?]
  J5 = Piezo Speaker
  Contrast1 = Trimmer Potentiometer [maximum_resistance=10kΩ package=THT]
  Q1 = PNP-Transistor [package="TO92 [THT]"]
  R6 = Resistor [tolerance=±5% resistance=220 package=THT]

nets:
  GND: LCD1.VSS, LCD1.R/W, Bauteil2.GND, J1.pin2, J3.pin1, J3.pin2, J3.pin3, J3.pin4, J5.pin1, Contrast1.leg1
  5V: LCD1.VDD, R2.Pin_1, Bauteil2.5V, J2.pin1, J2.pin2, J2.pin3, J2.pin4, R3.Pin_0, LED2.anode, LED1.anode, Contrast1.leg2
  N1: LCD1.V0, Contrast1.wiper
  N2: LCD1.RS, Bauteil2.D10
  N3: LCD1.E, Bauteil2.D9
  N4: LCD1.DB4, Bauteil2.D8
  N5: LCD1.DB5, Bauteil2.D7
  N6: LCD1.DB6, Bauteil2.D6
  N7: LCD1.DB7, Bauteil2.D5
  N8: LCD1.LED+, R2.Pin_0
  N9: LCD1.LED-, Q1.C
  N10: Bauteil2.D2, U1.pin1
  N11: Bauteil2.D3, U1.pin2
  N12: Bauteil2.D4, U1.pin4
  N13: Bauteil2.D11/MOSI, J4.pin1, J4.pin2, J4.pin3, J4.pin4, R3.Pin_1
  N14: Bauteil2.VIN, J1.pin1
  N15: Bauteil2.A3, J5.pin2
  N16: Bauteil2.A2, R6.Pin_0
  N17: Bauteil2.A1, R4.Pin_0
  N18: Bauteil2.A0, R5.Pin_0
  N19: LED2.cathode, R5.Pin_1
  N20: LED1.cathode, R4.Pin_1
  N21: U1.pin3, U1.pin5, Q1.E
  N22: Q1.B, R6.Pin_1
